// Logisim project RAM Query.circ as structural Verilog
module Timer (
  input  in_1,
  input  in_2,
  input  in_3,
  input  [3:0] in_4,
  output out_5
);

  wire [3:0] counter_1_q;

  Counter #(.width(4), .max('hf)) counter_1 (
    .count(in_1), .Q(counter_1_q), .clk(in_3), .clr(in_2));  // open: load, D, carry
  Comparator #(.width(4)) comparator_1 (.a(in_4), .b(counter_1_q), .eq(out_5));  // open: gt, lt

  // Other names for the same wires on the sheet: clk = in_3; ready = out_5; reset = in_2; start = in_1;
  //   wait_time[3:0] = in_4

  // Notes on the sheet:
  //   Timer
endmodule

module Inverse (
  input  [31:0] in_1,
  output [31:0] out_2
);


  assign out_2 = {in_1[7:0], in_1[15:8], in_1[23:16], in_1[31:24]};

  // Notes on the sheet:
  //   Bytes Inverser
endmodule

module Read_Data (
  input  [31:0] bank0,
  input  [31:0] bank1,
  input  [31:0] bank2,
  input  [31:0] bank3,
  input  in_5,
  input  [31:0] Ram_Dir,
  input  [3:0] RT,
  input  in_8,
  input  in_9,
  output out_10,
  output [31:0] read_data,
  output out_12
);

  wire demultiplexer_1_out0, demultiplexer_1_out1, or_1_out, or_2_out, ready;
  wire [31:0] inverse_1_out_2, multiplexer_1_out;

  or or_1 (or_1_out, out_12, in_8);
  Timer timer_1 (.in_1(out_10), .in_2(or_1_out), .in_3(in_5), .out_5(ready), .in_4(RT));
  or or_2 (or_2_out, demultiplexer_1_out0, in_9);
  D_Flip_Flop d_ff_1 (.clk(in_5), .D(or_2_out), .Q(out_10), .reset(in_8));  // open: Qn, preset, en
  Multiplexer #(.select(2), .width(32), .enable("false")) multiplexer_1 (
    .in0(bank0), .in1(bank1), .in2(bank2), .in3(bank3), .out(multiplexer_1_out), .sel(Ram_Dir[3:2]));
  Demultiplexer #(.enable("false")) demultiplexer_1 (
    .out0(demultiplexer_1_out0), .out1(demultiplexer_1_out1), .in(out_10), .sel(ready));
  Inverse inverse_1 (.in_1(multiplexer_1_out), .out_2(inverse_1_out_2));
  Register #(.width(32)) register_1 (.D(inverse_1_out_2), .en(out_10), .Q(read_data), .clk(in_5), .clr(in_8));
  D_Flip_Flop d_ff_2 (.clk(in_5), .D(demultiplexer_1_out1), .Q(out_12), .reset(in_8));  // open: Qn, preset, en

  // Other names for the same wires on the sheet: Clk = in_5; CS = out_10; data[31:0] = read_data; get = in_9;
  //   Selector[1:0] = Ram_Dir[3:2]; Read_Time[3:0] = RT; ready_read = out_12; reset = in_8

  // Notes on the sheet:
  //   Input
  //   Output
  //   RAM Reader
endmodule

module Write_Data (
  input  [31:0] in_1,
  input  [31:0] in_2,
  input  in_3,
  input  [3:0] in_4,
  input  in_5,
  input  in_6,
  output [31:0] out_7,
  output [31:0] out_8,
  output [31:0] out_9,
  output [31:0] out_10,
  output out_11,
  output out_12
);

  wire demultiplexer_1_out0, demultiplexer_1_out1, or_1_out, or_2_out, Ready;
  wire [31:0] inverse_1_out_2;

  or or_1 (or_1_out, demultiplexer_1_out0, in_6);
  D_Flip_Flop d_ff_1 (.clk(in_3), .D(or_1_out), .Q(out_11), .reset(in_5));  // open: Qn, preset, en
  or or_2 (or_2_out, in_5, out_12);
  Demultiplexer #(.enable("false")) demultiplexer_1 (
    .out0(demultiplexer_1_out0), .out1(demultiplexer_1_out1), .in(out_11), .sel(Ready));
  Timer timer_1 (.in_1(out_11), .in_2(or_2_out), .in_3(in_3), .out_5(Ready), .in_4(in_4));
  Inverse inverse_1 (.in_1(in_2), .out_2(inverse_1_out_2));
  D_Flip_Flop d_ff_2 (.clk(in_3), .D(demultiplexer_1_out1), .Q(out_12), .reset(in_5));  // open: Qn, preset, en
  Demultiplexer #(.select(2), .width(32), .enable("false")) demultiplexer_2 (
    .out0(out_7), .out1(out_8), .out2(out_9), .out3(out_10), .in(inverse_1_out_2), .sel(in_1[3:2]));

  // Other names for the same wires on the sheet: Bank0[31:0] = out_7; Bank1[31:0] = out_8; Bank2[31:0] = out_9;
  //   Bank3[31:0] = out_10; Clk = in_3; RAM_Dir[1:0] = in_1[3:2]; R_W = out_11; Ready_Write = out_12; Reset = in_5;
  //   Value[31:0] = in_2; Write = in_6; Write_Time[3:0] = in_4

  // Notes on the sheet:
  //   Input
  //   Output
  //   RAM Writer
endmodule
